# Fritzing sketch fan Sketch_12v-v1 (saved by Fritzing 1.0.0rc)
breadboards: 1

parts:
  Relay = RELAY [package=relay-jzc]
  12_V_Power_Supply = 2.1mm Barrel Jack with Terminal Block
  Part4 = Adafruit QT Py ESP32-S3 [part_number=5426]
  F1 = Fan - Ventilador [package=THT]
  12V_to_5V_buck_converter = RioRand LM2596

nets:
  N1: Relay.COIL2, Part4.+5V, 12V_to_5V_buck_converter.Pin_3
  N2: Relay.NC, Part4.SCK
  GND: Relay.NO, 12_V_Power_Supply.NEG, Part4.GND, F1.GND, 12V_to_5V_buck_converter.Pin_2, 12V_to_5V_buck_converter.Pin_4
  N3: Relay.MAIN, 12_V_Power_Supply.POS, 12V_to_5V_buck_converter.Pin_1
  N4: Relay.COIL1, F1.5V

notes:
  black - ground
  red - 12 v
  orange - 5v
  green - 3.3v
  resistor - 1k

custom parts:
  Adafruit QT Py ESP32-S3: The ESP32-S3 has arrived in QT Py format - and what a great way to get started with this powerful new chip from Espressif! With dual 240 MHz cores, WiFi and BLE support, and native USB, this QT Py is great for powering your IoT projects. The ESP32-S3 is a highly-integrated, low-power, 2.4 GHz Wi-Fi System-on-Chip (SoC) solution that now has WiFi and BLE support, built-in native USB as well as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
  Fan - Ventilador: Ventilador de 2 pines, se encuentra comunmente en computadoras de escritorio
